// Logisim project ExtendedCircuit_P20_G101.circ as structural Verilog: 3 circuits, main circuit main
module main (
  input  TOGGLE,
  input  in_2,
  input  in_3
);

  wire _0_out, _1_out, _2_out, _3_out, _4_out, _5_out, _6_out, _7_out, _8_out, _9_out, BCD_Sub_err,
       button_out, comparator_1_lt, DELAY_out_2, nor_1_out, not_1_out, not_2_out, or_1_out,
       priority_encoder_1_gs, SR_Latch_q, x_out;
  wire [0:0] adder_1_cout, adder_2_cout, not_3_out;
  wire [3:0] adder_1_out, adder_2_out, BCD_Sub_d0, BCD_Sub_d1, BCD_Sub_d2, BCD_Sub_d3, BCD_Sub_d4,
       BCD_Sub_d5, controlled_buffer_1_out, controlled_buffer_1_out_3, controlled_buffer_1_out_4, MRP_q_2,
       MRP_q_3, MRP_q_4, multiplexer_1_out, multiplexer_2_out, priority_encoder_1_out, VALUE_q_2, VALUE_q_3,
       VALUE_q_4, VALUE_q_5;
  wire [11:0] MRP_q;
  wire [23:0] shift_register_1_q0, VALUE_q;
  wire [23:8] controlled_buffer_1_out_2;

  Hex_Digit_Display hex_digit_display_1 (.value(VALUE_q[23:20]));  // open: dp
  Button _1 (.out(_1_out));
  Button _2 (.out(_2_out));
  Button _4 (.out(_4_out));
  Button _5 (.out(_5_out));
  Button _7 (.out(_7_out));
  Button _8 (.out(_8_out));
  Button _0 (.out(_0_out));
  Button x (.out(x_out));
  Hex_Digit_Display hex_digit_display_2 (.value(VALUE_q_5));  // open: dp
  Hex_Digit_Display hex_digit_display_3 (.value(VALUE_q_4));  // open: dp
  not not_1 (not_1_out, TOGGLE);
  Button _3 (.out(_3_out));
  Button _6 (.out(_6_out));
  Button _9 (.out(_9_out));
  Button button (.out(button_out));
  Hex_Digit_Display hex_digit_display_4 (.value(VALUE_q_3));  // open: dp
  Hex_Digit_Display hex_digit_display_5 (.value(VALUE_q_2));  // open: dp
  Hex_Digit_Display hex_digit_display_6 (.value(VALUE_q[3:0]));  // open: dp
  Register #(.width(24)) VALUE (
    .D(shift_register_1_q0), .en(not_1_out),
    .Q({VALUE_q[23:20], VALUE_q_5, VALUE_q_4, VALUE_q_3, VALUE_q_2, VALUE_q[3:0]}), .clk(not_2_out),
    .clr(in_2));
  not not_2 (not_2_out, priority_encoder_1_gs);
  Priority_Encoder #(.select(4)) priority_encoder_1 (
    .in0(_0_out), .in1(_1_out), .in2(_2_out), .in3(_3_out), .in4(_4_out), .in5(_5_out), .in6(_6_out),
    .in7(_7_out), .in8(_8_out), .in9(_9_out), .in10(1'b0), .in11(1'b0), .in12(1'b0), .in13(1'b0),
    .in14(1'b0), .in15(1'b0), .out(priority_encoder_1_out), .gs(priority_encoder_1_gs));  // open: en_out, en_in
  S_R_Flip_Flop SR_Latch (.Q(SR_Latch_q), .preset(button_out), .reset(x_out));  // open: S, clk, R, Qn, en
  Hex_Digit_Display hex_digit_display_7 (.value(MRP_q_3));  // open: dp
  Hex_Digit_Display hex_digit_display_8 (.value(MRP_q_4));  // open: dp
  Shift_Register #(.width(4), .length(6)) shift_register_1 (
    .shift(nor_1_out), .in(priority_encoder_1_out), .clk(priority_encoder_1_gs), .clr(x_out),
    .q0(shift_register_1_q0[3:0]), .q1(shift_register_1_q0[7:4]), .q2(shift_register_1_q0[11:8]),
    .q3(shift_register_1_q0[15:12]), .q4(shift_register_1_q0[19:16]), .q5(shift_register_1_q0[23:20]));  // open: out, load, d0, d1, d2, d3, d4, d5
  nor nor_1 (nor_1_out, SR_Latch_q, or_1_out);
  Hex_Digit_Display hex_digit_display_9 (.value(MRP_q[11:8]));  // open: dp
  Hex_Digit_Display hex_digit_display_10 (.value(MRP_q_2));  // open: dp
  Register #(.width(24)) MRP (
    .D(shift_register_1_q0), .en(TOGGLE), .Q({MRP_q_4, MRP_q_3, MRP_q_2, MRP_q}), .clk(not_2_out), .clr(in_3));
  or or_1 (or_1_out, shift_register_1_q0[23], shift_register_1_q0[22], shift_register_1_q0[21], shift_register_1_q0[20]);
  Hex_Digit_Display hex_digit_display_11 (.value(MRP_q[7:4]));  // open: dp
  Hex_Digit_Display hex_digit_display_12 (.value(MRP_q[3:0]));  // open: dp
  LED Bad_Input (.in(BCD_Sub_err));
  BCD_sub BCD_Sub (
    .A0(VALUE_q[3:0]), .B0(MRP_q[3:0]), .A1(VALUE_q_2), .B1(MRP_q[7:4]), .A2(VALUE_q_3), .B2(MRP_q[11:8]),
    .A3(VALUE_q_4), .B3(MRP_q_2), .A4(VALUE_q_5), .B4(MRP_q_3), .A5(VALUE_q[23:20]), .B5(MRP_q_4),
    .Enable(SR_Latch_q), .D0(BCD_Sub_d0), .D1(BCD_Sub_d1), .D2(BCD_Sub_d2), .D3(BCD_Sub_d3), .D4(BCD_Sub_d4),
    .D5(BCD_Sub_d5), .Err(BCD_Sub_err));
  assign {controlled_buffer_1_out_2[23:16], controlled_buffer_1_out_3, controlled_buffer_1_out_2[11:8], controlled_buffer_1_out, controlled_buffer_1_out_4} = DELAY_out_2 ? {BCD_Sub_d5, BCD_Sub_d4, BCD_Sub_d3, BCD_Sub_d2, BCD_Sub_d1, BCD_Sub_d0} : 24'bz;  // Controlled_Buffer controlled_buffer_1
  delay DELAY (.in_1(SR_Latch_q), .out_2(DELAY_out_2));
  Hex_Digit_Display hex_digit_display_13 (.value(controlled_buffer_1_out_2[19:16]));  // open: dp
  Hex_Digit_Display hex_digit_display_14 (.value(controlled_buffer_1_out_2[23:20]));  // open: dp
  Hex_Digit_Display hex_digit_display_15 (.value({3'b000, adder_1_cout[0]}));  // open: dp
  Hex_Digit_Display hex_digit_display_16 (.value(multiplexer_1_out));  // open: dp
  Multiplexer #(.width(4), .enable("false")) multiplexer_1 (
    .in0(controlled_buffer_1_out_3), .in1(adder_1_out), .out(multiplexer_1_out), .sel(adder_1_cout[0]));
  Adder #(.width(4)) adder_1 (
    .a(controlled_buffer_1_out_3), .b(4'b1010), .out(adder_1_out), .cin(1'b1), .cout(adder_1_cout[0]));
  Hex_Digit_Display hex_digit_display_17 (.value(controlled_buffer_1_out_2[11:8]));  // open: dp
  Hex_Digit_Display hex_digit_display_18 (.value({3'b000, adder_2_cout[0]}));  // open: dp
  Adder #(.width(4)) adder_2 (
    .a(controlled_buffer_1_out), .b(4'b1010), .out(adder_2_out), .cin(1'b1), .cout(adder_2_cout[0]));
  Multiplexer #(.width(4), .enable("false")) multiplexer_2 (
    .in0(controlled_buffer_1_out), .in1(adder_2_out), .out(multiplexer_2_out), .sel(adder_2_cout[0]));
  Hex_Digit_Display hex_digit_display_19 (.value({3'b000, not_3_out[0]}));  // open: dp
  not not_3 (not_3_out[0], comparator_1_lt);
  Comparator #(.mode("unsigned")) comparator_1 (
    .a({multiplexer_2_out, controlled_buffer_1_out_4}), .b(8'h25), .lt(comparator_1_lt));  // open: gt, eq

  // Notes on the sheet:
  //   CLEAR
  //   ENTER
  //   BCD
  //   trigger
  //   not 0
  //   #100
  //   #50
  //   #1
  //   #10
  //   #1
  //   #50p
  //   #25p
endmodule

module BCD_sub (
  input  [3:0] A0,
  input  [3:0] B0,
  input  [3:0] A1,
  input  [3:0] B1,
  input  [3:0] A2,
  input  [3:0] B2,
  input  [3:0] A3,
  input  [3:0] B3,
  input  [3:0] A4,
  input  [3:0] B4,
  input  [3:0] A5,
  input  [3:0] B5,
  input  Enable,
  output [3:0] D0,
  output [3:0] D1,
  output [3:0] D2,
  output [3:0] D3,
  output [3:0] D4,
  output [3:0] D5,
  output Err
);

  wire comparator_1_lt;
  wire [2:2] subtractor_1_bout, subtractor_2_bout, subtractor_3_bout, subtractor_4_bout, subtractor_5_bout,
       subtractor_6_bout;
  wire [3:0] subtractor_1_out, subtractor_2_out, subtractor_3_out, subtractor_4_out, subtractor_5_out,
       subtractor_6_out, subtractor_7_out, subtractor_8_out, subtractor_9_out, subtractor_10_out,
       subtractor_11_out, subtractor_12_out;

  Subtractor #(.width(4)) subtractor_1 (
    .a(A0), .b(B0), .out(subtractor_1_out), .bin(1'b0), .bout(subtractor_1_bout[2]));
  Subtractor #(.width(4)) subtractor_2 (
    .a(A1), .b(B1), .out(subtractor_2_out), .bin(subtractor_1_bout[2]), .bout(subtractor_2_bout[2]));
  Subtractor #(.width(4)) subtractor_3 (
    .a(A2), .b(B2), .out(subtractor_3_out), .bin(subtractor_2_bout[2]), .bout(subtractor_3_bout[2]));
  Subtractor #(.width(4)) subtractor_4 (
    .a(A3), .b(B3), .out(subtractor_4_out), .bin(subtractor_3_bout[2]), .bout(subtractor_4_bout[2]));
  Subtractor #(.width(4)) subtractor_5 (
    .a(A4), .b(B4), .out(subtractor_5_out), .bin(subtractor_4_bout[2]), .bout(subtractor_5_bout[2]));
  Subtractor #(.width(4)) subtractor_6 (
    .a(A5), .b(B5), .out(subtractor_6_out), .bin(subtractor_5_bout[2]), .bout(subtractor_6_bout[2]));
  Subtractor #(.width(4)) subtractor_7 (
    .a(subtractor_1_out), .b({1'b0, {2{subtractor_1_bout[2]}}, 1'b0}), .out(subtractor_7_out), .bin(1'b0));  // open: bout
  Subtractor #(.width(4)) subtractor_8 (
    .a(subtractor_2_out), .b({1'b0, {2{subtractor_2_bout[2]}}, 1'b0}), .out(subtractor_8_out), .bin(1'b0));  // open: bout
  Subtractor #(.width(4)) subtractor_9 (
    .a(subtractor_3_out), .b({1'b0, {2{subtractor_3_bout[2]}}, 1'b0}), .out(subtractor_9_out), .bin(1'b0));  // open: bout
  Subtractor #(.width(4)) subtractor_10 (
    .a(subtractor_4_out), .b({1'b0, {2{subtractor_4_bout[2]}}, 1'b0}), .out(subtractor_10_out), .bin(1'b0));  // open: bout
  Subtractor #(.width(4)) subtractor_11 (
    .a(subtractor_5_out), .b({1'b0, {2{subtractor_5_bout[2]}}, 1'b0}), .out(subtractor_11_out), .bin(1'b0));  // open: bout
  Subtractor #(.width(4)) subtractor_12 (
    .a(subtractor_6_out), .b({1'b0, {2{subtractor_6_bout[2]}}, 1'b0}), .out(subtractor_12_out), .bin(1'b0));  // open: bout
  Comparator #(.width(24), .mode("unsigned")) comparator_1 (
    .a({A5, A4, A3, A2, A1, A0}), .b({B5, B4, B3, B2, B1, B0}), .lt(comparator_1_lt));  // open: gt, eq
  or or_1 (Err, subtractor_6_bout[2], comparator_1_lt);
  Multiplexer #(.width(24), .disabled(0), .enable("false")) multiplexer_1 (
    .in0({A5, A4, A3, A2, A1, A0}),
    .in1({subtractor_12_out, subtractor_11_out, subtractor_10_out, subtractor_9_out, subtractor_8_out, subtractor_7_out}),
    .out({D5, D4, D3, D2, D1, D0}), .sel(Enable));
endmodule

module delay (
  input  in_1,
  output out_2
);

  wire not_1_out, not_2_out, not_3_out, not_4_out, not_6_out;

  not not_1 (not_1_out, in_1);
  not not_2 (not_2_out, not_1_out);
  not not_3 (not_3_out, not_4_out);
  not not_4 (not_4_out, not_6_out);
  not not_5 (out_2, not_3_out);
  not not_6 (not_6_out, not_2_out);
endmodule
