// Logisim project Main_P20_G101.circ as structural Verilog: 1 circuit, main circuit main
module main (
);

  wire _0_out, _1_out, _2_out, _3_out, _4_out, _5_out, _6_out, _7_out, _8_out, _9_out, button_out, nor_1_out,
       or_1_out, priority_encoder_1_gs, SR_Latch_q, x_out;
  wire [0:0] adder_1_cout;
  wire [3:0] adder_1_out, controlled_buffer_1_out, multiplexer_1_out, priority_encoder_1_out,
       shift_register_1_q0, shift_register_1_q1, shift_register_1_q2, shift_register_1_q3;
  wire [15:4] controlled_buffer_1_out_2;

  Button _2 (.out(_2_out));
  Button _3 (.out(_3_out));
  Button _1 (.out(_1_out));
  Button _5 (.out(_5_out));
  Button _4 (.out(_4_out));
  Button _6 (.out(_6_out));
  Button _9 (.out(_9_out));
  Button _7 (.out(_7_out));
  Button _8 (.out(_8_out));
  Button button (.out(button_out));
  Button _0 (.out(_0_out));
  Button x (.out(x_out));
  Priority_Encoder #(.select(4)) priority_encoder_1 (
    .in0(_0_out), .in1(_1_out), .in2(_2_out), .in3(_3_out), .in4(_4_out), .in5(_5_out), .in6(_6_out),
    .in7(_7_out), .in8(_8_out), .in9(_9_out), .in10(1'b0), .in11(1'b0), .in12(1'b0), .in13(1'b0),
    .in14(1'b0), .in15(1'b0), .out(priority_encoder_1_out), .gs(priority_encoder_1_gs));  // open: en_out, en_in
  S_R_Flip_Flop SR_Latch (.Q(SR_Latch_q), .preset(button_out), .reset(x_out));  // open: S, clk, R, Qn, en
  Hex_Digit_Display hex_digit_display_1 (.value(shift_register_1_q2));  // open: dp
  Hex_Digit_Display hex_digit_display_2 (.value(shift_register_1_q3));  // open: dp
  nor nor_1 (nor_1_out, SR_Latch_q, or_1_out);
  Hex_Digit_Display hex_digit_display_3 (.value(shift_register_1_q0));  // open: dp
  Hex_Digit_Display hex_digit_display_4 (.value(shift_register_1_q1));  // open: dp
  Shift_Register #(.width(4), .length(4)) shift_register_1 (
    .shift(nor_1_out), .in(priority_encoder_1_out), .clk(priority_encoder_1_gs), .clr(x_out),
    .q0(shift_register_1_q0), .q1(shift_register_1_q1), .q2(shift_register_1_q2), .q3(shift_register_1_q3));  // open: out, load, d0, d1, d2, d3
  or or_1 (or_1_out, shift_register_1_q3[3], shift_register_1_q3[2], shift_register_1_q3[1], shift_register_1_q3[0]);
  assign {controlled_buffer_1_out_2, controlled_buffer_1_out} = SR_Latch_q ? {shift_register_1_q3, shift_register_1_q2, shift_register_1_q1, shift_register_1_q0} : 16'bz;  // Controlled_Buffer controlled_buffer_1
  Hex_Digit_Display hex_digit_display_5 (.value(controlled_buffer_1_out_2[15:12]));  // open: dp
  Hex_Digit_Display hex_digit_display_6 (.value(controlled_buffer_1_out_2[11:8]));  // open: dp
  Hex_Digit_Display hex_digit_display_7 (.value({3'b000, adder_1_cout[0]}));  // open: dp
  Adder #(.width(4)) adder_1 (
    .a(controlled_buffer_1_out_2[7:4]), .b(4'b1010), .out(adder_1_out), .cin(1'b1), .cout(adder_1_cout[0]));
  Hex_Digit_Display hex_digit_display_8 (.value(multiplexer_1_out));  // open: dp
  Multiplexer #(.width(4), .enable("false")) multiplexer_1 (
    .in0(controlled_buffer_1_out_2[7:4]), .in1(adder_1_out), .out(multiplexer_1_out), .sel(adder_1_cout[0]));
  Hex_Digit_Display hex_digit_display_9 (.value(controlled_buffer_1_out));  // open: dp

  // Notes on the sheet:
  //   BCD
  //   trigger
  //   not 0
  //   #100
  //   #50
  //   #10
  //   #1
endmodule
